// Logisim project ex1.circ as structural Verilog: 1 circuit, main circuit generate_immediate
module generate_immediate (
  input  [31:0] INSTRUCTION,
  output [31:0] IMMEDIATE
);

  assign IMMEDIATE = {{20{INSTRUCTION[31]}}, {INSTRUCTION[31:25], INSTRUCTION[11:7]}};  // Bit_Extender bit_extender_1

  // Other names for the same wires on the sheet: TUN0[31:0] = IMMEDIATE
endmodule
