// Logisim project ex2.circ as structural Verilog: 1 circuit, main circuit compute_BrUn
module compute_BrUn (
  input  [31:0] INSTRUCTION,
  output BrUn
);

  wire comparator_1_eq;

  Comparator #(.mode("unsigned"), .width(7)) comparator_1 (
    .a(7'b1100011), .b(INSTRUCTION[6:0]), .eq(comparator_1_eq));  // open: gt, lt
  and and_1 (BrUn, comparator_1_eq, INSTRUCTION[13]);
endmodule
